# Fritzing sketch circuitDiagram (saved by Fritzing 0.9.3b)
breadboards: 1

parts:
  Bauteil2 = Ambient Light Sensor (TEMT6000 Breakout Board)
  T1 = LM35 Temperature Sensor [package="TO92 [THT]"]
  R1 = Resistor [tolerance=±5% resistance=1k package="2512 [SMD]"]
  WeMos_D1_Mini1 = WeMos D1 Mini  # not connected

nets:
  N1: Bauteil2.GND, R1.Pin_1
  N2: Bauteil2.S, T1.Vout
  N3: T1.GND, R1.Pin_0
